# Fritzing sketch attendance_makers_nios4 (saved by Fritzing 0.9.4)

parts:
  MCU1 = Raspberry Pi Zero
  LCM1602_IIC2 = LCM1602 IIC [part_number="LCM1602 IIC" chip_label="LCM1602 IIC" package="DIP (Dual Inline) [THT]"]
  Componente2 = RFID-RC522-v2
  LCD1 = 20x4 LCD display [part_number=2004A]

nets:
  N1: MCU1.pin_1, MCU1.pin_17, Componente2.3.3V
  N2: MCU1.pin_2, LCM1602_IIC2.VCC
  N3: MCU1.pin_3, LCM1602_IIC2.SDA
  N4: MCU1.pin_5, LCM1602_IIC2.SCL
  GND: MCU1.pin_6, MCU1.pin_25, MCU1.pin_39, LCM1602_IIC2.GND, Componente2.GND
  N5: MCU1.pin_19, Componente2.MOSI
  N6: MCU1.pin_21, Componente2.MISO
  N7: MCU1.pin_22, Componente2.RST
  N8: MCU1.pin_23, Componente2.SCK
  N9: MCU1.pin_24, Componente2.SDA
  VSS: LCM1602_IIC2.VSS, LCD1.Vss
  VDD: LCM1602_IIC2.VDD, LCD1.Vdd
  N10: LCM1602_IIC2.V0, LCD1.Vo
  N11: LCM1602_IIC2.RS, LCD1.RS
  N12: LCM1602_IIC2.RW, LCD1.R/W
  N13: LCM1602_IIC2.E, LCD1.E
  N14: LCM1602_IIC2.D0, LCD1.DB0
  N15: LCM1602_IIC2.D1, LCD1.DB1
  N16: LCM1602_IIC2.D2, LCD1.DB2
  N17: LCM1602_IIC2.D3, LCD1.DB3
  N18: LCM1602_IIC2.D4, LCD1.DB4
  N19: LCM1602_IIC2.D5, LCD1.DB5
  N20: LCM1602_IIC2.D6, LCD1.DB6
  N21: LCM1602_IIC2.D7, LCD1.DB7
  N22: LCM1602_IIC2.A, LCD1.A_+
  N23: LCM1602_IIC2.K, LCD1.K_-
  N24: LCM1602_IIC2.LED_A, LCM1602_IIC2.LED_B

custom parts:
  LCM1602 IIC: I2C-Module to use a 1602 or 2004 LCD on with the wire.h libory Serial LCD Modul
  RFID-RC522-v2: A simple China made RFID-RC522 Reader; do check the pin labels, as this is a MFRC522 based clone.
  20x4 LCD display: 20x4 character display. CHECK LED POLARITY BEFORE CONNECTING POWER Some versions of the dispaly have the polarity of the LED pins "A" and "K" reversed.
